# Fritzing sketch EsquemaMontagemProtoboard (saved by Fritzing 0.9.3b)
breadboards: 1

parts:
  Componente1 = Arduino Uno (Rev3)
  LED1 = LED - 5mm [color="Red (633nm)" package="5 mm [THT]"]
  LED2 = LED - 5mm [color="Green (555nm)" package="5 mm [THT]"]
  LED3 = LED - 5mm [color="Yellow (585nm)" package="5 mm [THT]"]
  R1 = Resistor [tolerance=±5% resistance=100 package="1206 [SMD]"]
  SG4 = Buzzer 12mm [package=buzzer-12mm-ns]
  R4 = Photocell (LDR) [package=THT]
  R5 = Resistor [tolerance=±5% resistance=220 package="1206 [SMD]"]
  U1 = POT [package=pot_alpha_rv16af-20]
  R6 = Resistor [tolerance=±5% resistance=10k package="1206 [SMD]"]
  R7 = Resistor [tolerance=±5% resistance=100 package="1206 [SMD]"]
  R8 = Resistor [tolerance=±5% resistance=100 package="1206 [SMD]"]
  LED4 = RGB LED (com. cathode, rbg) [package="5 mm [THT]"]
  R9 = Resistor [tolerance=±5% resistance=220 package="1206 [SMD]"]
  R10 = Resistor [tolerance=±5% resistance=220 package="1206 [SMD]"]
  S2 = Round Pushbutton
  R11 = Resistor [tolerance=±5% resistance=10k package="1206 [SMD]"]

nets:
  N1: Componente1.A0, R4.pin_1, R6.Pin_1
  N2: Componente1.A1, U1.S
  N3: Componente1.D9_PWM, R10.Pin_0
  N4: Componente1.D10_PWM/SS, R9.Pin_0
  N5: Componente1.D11_PWM/MOSI, R5.Pin_0
  N6: Componente1.GND, LED1.cathode, LED2.cathode, LED3.cathode, SG4.2, U1.A, R6.Pin_0, LED4.common_cathode, R11.Pin_0
  N7: Componente1.D2, S2.leg0, R11.Pin_1
  N8: Componente1.D3_PWM, SG4.1
  N9: Componente1.D5_PWM, R8.Pin_0
  N10: Componente1.D6_PWM, R7.Pin_0
  N11: Componente1.D7, R1.Pin_0
  N12: Componente1.5V, R4.pin_0, U1.E, S2.leg1
  N13: LED1.anode, R1.Pin_1
  N14: LED2.anode, R8.Pin_1
  N15: LED3.anode, R7.Pin_1
  N16: R5.Pin_1, LED4.red_anode
  N17: LED4.blue_anode, R9.Pin_1
  N18: LED4.green_anode, R10.Pin_1
